# Fritzing sketch traethlin (saved by Fritzing 0.9.6b)

parts:
  Mod1 = Raspberry Pi 4B
  A1 = ESP32 Wroom 32E dev board
  Steering = Basic Servo
  Front_diff = Basic Servo
  Rear_diff = Basic Servo
  ESC = Dagu DGServo 9g header connector (female) [package=THT]
  DC1 = DC_DC_XL4016 [package=board_screw]
  Gearbox = Basic Servo
  5V = Screw terminal - 2 pins [package=THT]
  3_3V = Screw terminal - 2 pins [package=THT]
  GND = Screw terminal - 2 pins [package=THT]
  U1 = WS2812 RGB LED strip
  Part1 = Adafruit BNO055 STEMMA QT [part_number="Adafruit #4646"]
  Part2 = Adafruit MLX90640 Thermal Camera [part_number="Adafruit #4407"]
  Front_water_probe = Screw terminal - 2 pins [package=THT]
  Rear_water_probe = Screw terminal - 2 pins [package=THT]
  R1 = Resistor [tolerance=±5% resistance=1M power=0.25 package="0402 [SMD]"]
  R2 = Resistor [tolerance=±5% resistance=1M power=0.25 package="0402 [SMD]"]
  Lipo_battery_connector = Screw terminal - 2 pins [package=THT]

nets (from the breadboard view):
  3V3: Mod1.3V3, Part1.VCC
  VCC: Mod1.5V, DC1.OUT+, 5V.pin1, 5V.pin2, U1.VCC, Part2.VCC
  GND: Mod1.GND, A1.Pin_14, A1.Pin_38, DC1.OUT-, GND.pin1, GND.pin2, U1.GND, Part1.GND, Part2.GND
  N1: Mod1.GPIO4, A1.Pin_10
  N2: Mod1.GPIO7, A1.Pin_8
  N3: Mod1.ID_SD, Part1.SCL
  N4: Mod1.ID_SC, Part1.SDA
  N5: Mod1.GPIO5, A1.Pin_11
  N6: Mod1.GPIO6, A1.Pin_12
  N7: Mod1.GPIO26, A1.Pin_24
  N8: A1.Pin_1, 3_3V.pin1, 3_3V.pin2, R1.Pin_1, R2.Pin_1
  N9: A1.Pin_15, Rear_water_probe.pin1, R1.Pin_0
  N10: A1.Pin_26, Front_water_probe.pin1, R2.Pin_0
  N11: A1.Pin_27, Steering.pulse
  N12: A1.Pin_28, ESC.pulse
  N13: A1.Pin_29, Front_diff.pulse
  N14: A1.Pin_30, Rear_diff.pulse
  N15: A1.Pin_31, Gearbox.pulse
  N16: A1.Pin_33, Part2.SDA
  N17: A1.Pin_36, Part2.SCL
  N18: A1.Pin_37, U1.DIN
  VCC_2: Steering.vcc, Front_diff.vcc, Rear_diff.vcc, ESC.Vcc, Gearbox.vcc
  GND_2: Rear_diff.gnd, ESC.gnd, Gearbox.gnd
  N19: DC1.IN+, Lipo_battery_connector.pin2
  N20: DC1.IN-, Lipo_battery_connector.pin1
  N21: Front_water_probe.pin2, Rear_water_probe.pin2

custom parts:
  ESP32 Wroom 32E dev board: The ESP32 WROOM-32E is a versatile and powerful module built around Espressif’s ESP32 chipset. It offers dual-core processing, integrated Wi-Fi and Bluetooth connectivity, and boasts a wide range of peripheral interfaces.
  WS2812 RGB LED strip: WS2812 strip
  Adafruit BNO055 STEMMA QT: If you've ever ordered and wire up a 9-DOF sensor, chances are you've also realized the challenge of turning the sensor data from an accelerometer, gyroscope, and magnetometer into actual "3D space orientation"! Orientation is a hard problem to solve. The sensor fusion algorithms (the secret sauce that blends accelerometer, magnetometer, and gyroscope data into stable three-axis orientation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
  Adafruit MLX90640 Thermal Camera: You can now add affordable heat-vision to your project and with an Adafruit MLX90640 Thermal Camera Breakout. This sensor contains a 24x32 array of IR thermal sensors. When connected to your microcontroller (or Raspberry Pi) it will return an array of 768 individual infrared temperature readings over I2C. It's like those fancy thermal cameras, but compact and simple enough for easy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
